# Fritzing sketch Diamgram_esp32 (saved by Fritzing 0.9.3b)
breadboards: 1

parts:
  uPesy_ESP32_Wroom_DevKit1 = uPesy ESP32 Wroom Low Power DevKit
  Composant1 = Adafruit BME680 [part_number="Adafruit #3660"]
  M1 = Osoyoo SX1278-ra-02

nets:
  N1: uPesy_ESP32_Wroom_DevKit1.GPIO23, M1.MOSI
  N2: uPesy_ESP32_Wroom_DevKit1.GPIO22, Composant1.SCK/SCL
  N3: uPesy_ESP32_Wroom_DevKit1.GPIO21, Composant1.SDI/SDA
  N4: uPesy_ESP32_Wroom_DevKit1.GPIO19, M1.MISO
  N5: uPesy_ESP32_Wroom_DevKit1.GPIO18, M1.SCK
  N6: uPesy_ESP32_Wroom_DevKit1.GPIO5, M1.NSS
  N7: uPesy_ESP32_Wroom_DevKit1.GPIO4, M1.DIO0
  N8: uPesy_ESP32_Wroom_DevKit1.GPIO2, M1.DIO1
  3V3: uPesy_ESP32_Wroom_DevKit1.3V3, M1.3.3V
  GND: uPesy_ESP32_Wroom_DevKit1.GND, Composant1.GND, M1.GND
  N9: uPesy_ESP32_Wroom_DevKit1.GPIO14, M1.RST
  N10: uPesy_ESP32_Wroom_DevKit1.GPIO32, Composant1.3.3V

custom parts:
  uPesy ESP32 Wroom Low Power DevKit: ESP32 development board that is 100% breadboard compatible
  Osoyoo SX1278-ra-02: Osoyoo Long Distance wireless transceiver Uart LoRa Module.
